// Logisim project F6.circ as structural Verilog: 5 circuits, main circuit main
module main (
  input  EN,
  input  rst
);

  wire clk_out;
  wire [31:0] pc_1_pc_out, rom_1_data;

  Clock clk (.out(clk_out));
  PC pc_1 (.EN(EN), .clk(clk_out), .rst(rst), .PC_out(pc_1_pc_out));  // open: PC_in, PC_select
  ROM #(.addrWidth(24), .dataWidth(32)) rom_1 (.addr(pc_1_pc_out[23:0]), .data(rom_1_data));
  Controller controller_1 (
    .opcode(rom_1_data[6:0]), .funct3(rom_1_data[14:12]), .funct7(rom_1_data[31:25]));  // open: PC_select

  // Notes on the sheet:
  //   add, addi, lui, lw, lbu, sw, sb, jalr
endmodule

module PC (
  input  [31:0] PC_in,
  input  PC_select,
  input  EN,
  input  clk,
  input  rst,
  output [31:0] PC_out
);

  wire [31:0] adder_1_out, multiplexer_1_out;

  Register #(.width(32)) register_1 (.D(multiplexer_1_out), .en(EN), .clk(clk), .Q(PC_out), .clr(rst));
  Multiplexer #(.width(32)) multiplexer_1 (.in0(PC_in), .in1(adder_1_out), .out(multiplexer_1_out), .sel(PC_select));
  Adder #(.width(32)) adder_1 (.a(PC_out), .b(32'h4), .out(adder_1_out));  // open: cin, cout

  // Notes on the sheet:
  //   add, addi, lui, lw, lbu, sw, sb, jalr
endmodule

module Fetch (
);
endmodule

module Controller (
  input  [6:0] opcode,
  input  [2:0] funct3,
  input  [6:0] funct7,
  output PC_select
);
endmodule

module Registers (
  input  clk,
  input  rst,
  input  [3:0] rdR,
  input  [31:0] rdD,
  input  wEN,
  input  [3:0] rs1R,
  input  [3:0] rs2R,
  output [31:0] rs1D,
  output [31:0] rs2D
);

  wire and_1_out, and_2_out, and_3_out, and_4_out, and_5_out, and_6_out, and_7_out, and_8_out, and_9_out,
       and_10_out, and_11_out, and_12_out, and_13_out, and_14_out, and_15_out, and_16_out, decoder_1_out0,
       decoder_1_out1, decoder_1_out2, decoder_1_out3, decoder_2_out0, decoder_2_out1, decoder_2_out2,
       decoder_2_out3;
  wire [31:0] R0_q, R1_q, R2_q, R3_q, R4_q, R5_q, R6_q, R7_q, R8_q, R9_q, R10_q, R11_q, R12_q, R13_q, R14_q,
       R15_q;

  Decoder #(.select(2)) decoder_1 (
    .out0(decoder_1_out0), .out1(decoder_1_out1), .out2(decoder_1_out2), .out3(decoder_1_out3),
    .sel(rdR[3:2]), .en(wEN));
  Decoder #(.select(2)) decoder_2 (
    .out0(decoder_2_out0), .out1(decoder_2_out1), .out2(decoder_2_out2), .out3(decoder_2_out3),
    .sel(rdR[1:0]), .en(wEN));
  and and_1 (and_1_out, decoder_2_out0, decoder_1_out0);
  and and_2 (and_2_out, decoder_2_out1, decoder_1_out0);
  and and_3 (and_3_out, decoder_2_out2, decoder_1_out0);
  and and_4 (and_4_out, decoder_2_out3, decoder_1_out0);
  Register #(.width(32)) R0 (.D(rdD), .en(and_1_out), .clk(clk), .Q(R0_q), .clr(rst));
  Register #(.width(32)) R1 (.D(rdD), .en(and_2_out), .clk(clk), .Q(R1_q), .clr(rst));
  Register #(.width(32)) R2 (.D(rdD), .en(and_3_out), .clk(clk), .Q(R2_q), .clr(rst));
  Register #(.width(32)) R3 (.D(rdD), .en(and_4_out), .clk(clk), .Q(R3_q), .clr(rst));
  Register #(.width(32)) R4 (.D(rdD), .en(and_5_out), .clk(clk), .Q(R4_q), .clr(rst));
  and and_5 (and_5_out, decoder_2_out0, decoder_1_out1);
  Register #(.width(32)) R5 (.D(rdD), .en(and_6_out), .clk(clk), .Q(R5_q), .clr(rst));
  and and_6 (and_6_out, decoder_2_out1, decoder_1_out1);
  Register #(.width(32)) R6 (.D(rdD), .en(and_7_out), .clk(clk), .Q(R6_q), .clr(rst));
  and and_7 (and_7_out, decoder_2_out2, decoder_1_out1);
  Register #(.width(32)) R7 (.D(rdD), .en(and_8_out), .clk(clk), .Q(R7_q), .clr(rst));
  and and_8 (and_8_out, decoder_2_out3, decoder_1_out1);
  Register #(.width(32)) R8 (.D(rdD), .en(and_9_out), .clk(clk), .Q(R8_q), .clr(rst));
  and and_9 (and_9_out, decoder_2_out0, decoder_1_out2);
  Register #(.width(32)) R9 (.D(rdD), .en(and_10_out), .clk(clk), .Q(R9_q), .clr(rst));
  and and_10 (and_10_out, decoder_2_out1, decoder_1_out2);
  Register #(.width(32)) R10 (.D(rdD), .en(and_11_out), .clk(clk), .Q(R10_q), .clr(rst));
  and and_11 (and_11_out, decoder_2_out2, decoder_1_out2);
  Register #(.width(32)) R11 (.D(rdD), .en(and_12_out), .clk(clk), .Q(R11_q), .clr(rst));
  and and_12 (and_12_out, decoder_2_out3, decoder_1_out2);
  and and_13 (and_13_out, decoder_2_out0, decoder_1_out3);
  and and_14 (and_14_out, decoder_2_out1, decoder_1_out3);
  and and_15 (and_15_out, decoder_2_out2, decoder_1_out3);
  and and_16 (and_16_out, decoder_2_out3, decoder_1_out3);
  Register #(.width(32)) R12 (.D(rdD), .en(and_13_out), .clk(clk), .Q(R12_q), .clr(rst));
  Register #(.width(32)) R13 (.D(rdD), .en(and_14_out), .clk(clk), .Q(R13_q), .clr(rst));
  Register #(.width(32)) R14 (.D(rdD), .en(and_15_out), .clk(clk), .Q(R14_q), .clr(rst));
  Register #(.width(32)) R15 (.D(rdD), .en(and_16_out), .clk(clk), .Q(R15_q), .clr(rst));
  Multiplexer #(.select(2), .width(32)) multiplexer_1 (
    .in0(R0_q), .in1(R4_q), .in2(R8_q), .in3(R12_q));  // open: out, sel
  Multiplexer #(.select(2), .width(32)) multiplexer_2 (
    .in0(R1_q), .in1(R5_q), .in2(R9_q), .in3(R13_q));  // open: out, sel
  Multiplexer #(.select(2), .width(32)) multiplexer_3 (
    .in0(R2_q), .in1(R6_q), .in2(R10_q), .in3(R14_q));  // open: out, sel
  Multiplexer #(.select(2), .width(32)) multiplexer_4 (
    .in0(R3_q), .in1(R7_q), .in2(R11_q), .in3(R15_q));  // open: out, sel
endmodule
